// Logisim project 22.11.2021.circ as structural Verilog: 4 circuits, main circuit main
module main (
  input  a,
  input  b,
  input  c,
  output y
);

  wire and_1_out_3, and_2_out_3, not_1_out_2, or_1_out_3, xor_1_out;

  \not  not_1 (.in_1(b), .out_2(not_1_out_2));
  \and  and_1 (.in_1(a), .in_2(not_1_out_2), .out_3(and_1_out_3));
  \and  and_2 (.in_1(and_1_out_3), .in_2(c), .out_3(and_2_out_3));
  \or  or_1 (.in_1(and_2_out_3), .in_2(xor_1_out), .out_3(or_1_out_3));
  xor xor_1 (xor_1_out, a, b);
  \or  or_2 (.in_1(or_1_out_3), .in_2(c), .out_3(y));
endmodule

module \not  (
  input  in_1,
  output out_2
);

  nand nand_1 (out_2, in_1, in_1);
endmodule

module \and  (
  input  in_1,
  input  in_2,
  output out_3
);

  wire nand_1_out;

  nand nand_1 (nand_1_out, in_1, in_2);
  nand nand_2 (out_3, nand_1_out, nand_1_out);
endmodule

module \or  (
  input  in_1,
  input  in_2,
  output out_3
);

  wire nand_1_out, nand_2_out;

  nand nand_1 (nand_1_out, in_1, in_1);
  nand nand_2 (nand_2_out, in_2, in_2);
  nand nand_3 (out_3, nand_1_out, nand_2_out);
endmodule
