// Logisim project firstlogism.circ as structural Verilog: 6 circuits, main circuit main
module main (
  input  a,
  input  b,
  input  c,
  output y
);

  wire not_out_2, or_2_out_3, or_3_out_3, or_out_3, xor_1_out_3;

  \not  \not  (.in_1(b), .out_2(not_out_2));
  \xor  xor_1 (.in_1(b), .in_2(a), .out_3(xor_1_out_3));
  \and  \or  (.in_1(a), .in_2(not_out_2), .out_3(or_out_3));
  \and  or_2 (.in_1(or_out_3), .in_2(c), .out_3(or_2_out_3));
  \or  or_3 (.in_1(xor_1_out_3), .in_2(or_2_out_3), .out_3(or_3_out_3));
  \or  or_4 (.in_1(or_3_out_3), .in_2(c), .out_3(y));
endmodule

module \not  (
  input  in_1,
  output out_2
);

  nand nand_1 (out_2, in_1, in_1);
endmodule

module \and  (
  input  in_1,
  input  in_2,
  output out_3
);

  wire nand_1_out;

  nand nand_1 (nand_1_out, in_1, in_2);
  nand nand_2 (out_3, nand_1_out, nand_1_out);
endmodule

module \or  (
  input  in_1,
  input  in_2,
  output out_3
);

  wire nand_1_out, nand_2_out;

  nand nand_1 (nand_1_out, in_1, in_1);
  nand nand_2 (nand_2_out, in_2, in_2);
  nand nand_3 (out_3, nand_1_out, nand_2_out);
endmodule

module \xor  (
  input  in_1,
  input  in_2,
  output out_3
);

  wire nand_1_out, nand_2_out, nand_3_out;

  nand nand_1 (nand_1_out, in_1, in_2);
  nand nand_2 (nand_2_out, in_1, nand_1_out);
  nand nand_3 (nand_3_out, nand_1_out, in_2);
  nand nand_4 (out_3, nand_2_out, nand_3_out);
endmodule

module test (
  input  a,
  input  b,
  input  c,
  output x,
  output y
);

  wire not_out_2, or_2_out_3, or_3_out_3, or_out_3, xor_1_out_3;

  main main_1 (.a(a), .b(b), .c(c), .y(x));
  \not  \not  (.in_1(b), .out_2(not_out_2));
  \and  \or  (.in_1(a), .in_2(not_out_2), .out_3(or_out_3));
  \xor  xor_1 (.in_1(b), .in_2(a), .out_3(xor_1_out_3));
  \or  or_2 (.in_1(xor_1_out_3), .in_2(or_3_out_3), .out_3(or_2_out_3));
  \and  or_3 (.in_1(or_out_3), .in_2(c), .out_3(or_3_out_3));
  \or  or_4 (.in_1(or_2_out_3), .in_2(c), .out_3(y));
endmodule
