// Logisim project fiveth.circ as structural Verilog: 2 circuits, main circuit main
module main (
  input  sygnal_wyjscowy
);

  wire and_1_out, and_2_out, and_3_out, and_5_out, and_6_out, and_7_out, and_8_out, clock_1_out, d_ff_1_q,
       d_ff_1_qn, d_ff_2_q, d_ff_2_qn, not_1_out, or_1_out, or_2_out;

  Clock clock_1 (.out(clock_1_out));
  D_Flip_Flop d_ff_1 (.clk(clock_1_out), .D(d_ff_1_qn), .Q(d_ff_1_q), .Qn(d_ff_1_qn));  // open: preset, en, reset
  D_Flip_Flop d_ff_2 (.clk(d_ff_1_qn), .D(d_ff_2_qn), .Q(d_ff_2_q), .Qn(d_ff_2_qn));  // open: preset, en, reset
  not not_1 (not_1_out, d_ff_2_q);
  and and_1 (and_1_out, ~d_ff_1_q, d_ff_2_q);  // AND_Gate
  and and_2 (and_2_out, not_1_out, sygnal_wyjscowy);
  and and_3 (and_3_out, and_1_out, sygnal_wyjscowy);
  LED led_1 (.in(and_2_out));
  LED led_2 (.in(and_8_out));
  LED led_3 (.in(and_3_out));
  // AND_Gate and_4 has open pins: in0=sygnal_wyjscowy, in1=clock_1_out, out=open
  and and_5 (and_5_out, ~d_ff_1_q, d_ff_2_q);  // AND_Gate
  or or_1 (or_1_out, and_5_out, and_6_out);
  and and_6 (and_6_out, d_ff_1_q, ~d_ff_2_q);  // AND_Gate
  and and_7 (and_7_out, or_1_out, ~sygnal_wyjscowy);  // AND_Gate
  and and_8 (and_8_out, clock_1_out, or_2_out);
  or or_2 (or_2_out, d_ff_1_q, and_7_out);
endmodule

module \тест  (
  input  in_1,
  input  in_2,
  output out_3
);

  or or_1 (out_3, in_1, ~in_2);  // OR_Gate
endmodule
