// Logisim project fourth.circ as structural Verilog: 4 circuits, main circuit main
module main (
);

  wire and_1_out, clock_1_out, d_ff_1_qn, d_ff_2_qn, d_ff_3_qn, d_ff_4_qn;
  wire [3:0] d_ff_1_q;

  Hex_Digit_Display hex_digit_display_1 (.value(d_ff_1_q));  // open: dp
  Clock clock_1 (.out(clock_1_out));
  D_Flip_Flop d_ff_1 (
    .clk(clock_1_out), .D(d_ff_1_qn), .Q(d_ff_1_q[0]), .Qn(d_ff_1_qn), .reset(and_1_out));  // open: preset, en
  and and_1 (and_1_out, d_ff_1_q[1], d_ff_1_q[3]);
  D_Flip_Flop d_ff_2 (
    .clk(d_ff_1_qn), .D(d_ff_2_qn), .Q(d_ff_1_q[1]), .Qn(d_ff_2_qn), .reset(and_1_out));  // open: preset, en
  D_Flip_Flop d_ff_3 (
    .clk(d_ff_2_qn), .D(d_ff_3_qn), .Q(d_ff_1_q[2]), .Qn(d_ff_3_qn), .reset(and_1_out));  // open: preset, en
  D_Flip_Flop d_ff_4 (
    .clk(d_ff_3_qn), .D(d_ff_4_qn), .Q(d_ff_1_q[3]), .Qn(d_ff_4_qn), .reset(and_1_out));  // open: preset, en
endmodule

module _6 (
  output out_1,
  output out_2,
  output out_3,
  output out_4
);

  wire clock_1_out, d_ff_4_qn, xor_1_out;

  Clock clock_1 (.out(clock_1_out));
  ExactlyOne xor_1 (.out(xor_1_out), .in0(out_2), .in2(out_1), .in3(d_ff_4_qn));
  D_Flip_Flop d_ff_1 (.clk(clock_1_out), .D(out_1), .Q(out_2));  // open: Qn, preset, en, reset
  D_Flip_Flop d_ff_2 (.clk(clock_1_out), .D(xor_1_out), .Q(out_1));  // open: Qn, preset, en, reset
  D_Flip_Flop d_ff_3 (.clk(clock_1_out), .D(out_2), .Q(out_3));  // open: Qn, preset, en, reset
  D_Flip_Flop d_ff_4 (.clk(clock_1_out), .D(out_3), .Q(out_4), .Qn(d_ff_4_qn));  // open: preset, en, reset
endmodule

module _7 (
  input  in_1,
  input  in_2,
  output out_3,
  output out_4
);

  wire clock_1_out, nand_1_out, nand_2_out;

  Clock clock_1 (.out(clock_1_out));
  nand nand_1 (nand_1_out, in_1, clock_1_out);
  nand nand_2 (nand_2_out, clock_1_out, in_2);
  nand nand_3 (out_3, out_4, nand_1_out);
  nand nand_4 (out_4, nand_2_out, out_3);
endmodule

module _8 (
  input  in_1,
  input  in_2,
  output out_3,
  output out_4,
  output out_5,
  output out_6
);

  wire clock_1_out, d_ff_1_q, d_ff_2_q, d_ff_3_q, d_ff_4_q, d_ff_4_qn;

  Clock clock_1 (.out(clock_1_out));
  D_Flip_Flop d_ff_1 (.clk(clock_1_out), .D(d_ff_4_qn), .Q(d_ff_1_q), .preset(in_2));  // open: Qn, en, reset
  _7 u_7_1 (.in_1(clock_1_out), .in_2(in_1), .out_3(out_3));  // open: out_4
  D_Flip_Flop d_ff_2 (.clk(clock_1_out), .D(d_ff_1_q), .Q(d_ff_2_q), .reset(in_2));  // open: Qn, preset, en
  _7 u_7_2 (.in_1(clock_1_out), .in_2(in_1), .out_3(out_4));  // open: out_4
  D_Flip_Flop d_ff_3 (.clk(clock_1_out), .D(d_ff_2_q), .Q(d_ff_3_q), .reset(in_2));  // open: Qn, preset, en
  _7 u_7_3 (.in_1(clock_1_out), .in_2(in_1), .out_3(out_5));  // open: out_4
  _7 u_7_4 (.in_1(d_ff_4_q), .in_2(in_1), .out_3(out_6));  // open: out_4
  D_Flip_Flop d_ff_4 (.clk(clock_1_out), .D(d_ff_3_q), .Q(d_ff_4_q), .Qn(d_ff_4_qn), .reset(in_2));  // open: preset, en
endmodule
