// Logisim project syc20212911.circ as structural Verilog: 8 circuits, main circuit main
module main (
  input  a,
  input  b,
  input  c,
  input  d,
  output out_5
);

  wire and_1_out_5, and_2_out_5, and_3_out_5, and_4_out_5, not_1_out_2, not_2_out_2, not_3_out_2,
       not_4_out_2, not_5_out_2, not_6_out_2, not_7_out_2;

  \not  not_1 (.in_1(a), .out_2(not_1_out_2));
  \not  not_2 (.in_1(b), .out_2(not_2_out_2));
  \not  not_3 (.in_1(a), .out_2(not_3_out_2));
  \not  not_4 (.in_1(b), .out_2(not_4_out_2));
  \not  not_5 (.in_1(c), .out_2(not_5_out_2));
  \not  not_6 (.in_1(c), .out_2(not_6_out_2));
  \not  not_7 (.in_1(c), .out_2(not_7_out_2));
  \and  and_1 (.in_1(not_1_out_2), .in_2(not_2_out_2), .in_3(not_6_out_2), .in_4(d), .out_5(and_1_out_5));
  \and  and_2 (.in_1(not_3_out_2), .in_2(b), .in_3(c), .in_4(d), .out_5(and_2_out_5));
  \and  and_3 (.in_1(a), .in_2(not_4_out_2), .in_3(not_7_out_2), .in_4(d), .out_5(and_3_out_5));
  \and  and_4 (.in_1(a), .in_2(b), .in_3(not_5_out_2), .in_4(d), .out_5(and_4_out_5));
  \or  or_1 (.in_1(and_1_out_5), .in_2(and_2_out_5), .in_3(and_3_out_5), .in_4(and_4_out_5), .out_5(out_5));
endmodule

module main2 (
  input  l,
  input  f,
  input  r,
  output leftEngine,
  output rightEngine
);

  wire andfromnor_1_out_3, andfromnor_2_out_3, andfromnor_3_out_3, andfromnor_4_out_3, andfromnor_5_out_3,
       andfromnor_6_out_3, andfromnor_8_out_3, notfromnor_1_out_2, notfromnor_2_out_2, notfromnor_3_out_2,
       notfromnor_4_out_2, notfromnor_5_out_2, orfromnor_1_out_3, orfromnor_2_out_3;

  andfromnor andfromnor_1 (.in_1(l), .in_2(f), .out_3(andfromnor_1_out_3));
  notfromnor notfromnor_1 (.in_1(f), .out_2(notfromnor_1_out_2));
  andfromnor andfromnor_2 (.in_1(f), .in_2(r), .out_3(andfromnor_2_out_3));
  andfromnor andfromnor_3 (.in_1(r), .in_2(f), .out_3(andfromnor_3_out_3));
  andfromnor andfromnor_4 (.in_1(andfromnor_3_out_3), .in_2(l), .out_3(andfromnor_4_out_3));
  andfromnor andfromnor_5 (.in_1(notfromnor_2_out_2), .in_2(f), .out_3(andfromnor_5_out_3));
  notfromnor notfromnor_2 (.in_1(r), .out_2(notfromnor_2_out_2));
  notfromnor notfromnor_3 (.in_1(l), .out_2(notfromnor_3_out_2));
  andfromnor andfromnor_6 (.in_1(andfromnor_5_out_3), .in_2(notfromnor_3_out_2), .out_3(andfromnor_6_out_3));
  orfromnor orfromnor_1 (.in_1(andfromnor_1_out_3), .in_2(notfromnor_1_out_2), .out_3(orfromnor_1_out_3));
  orfromnor orfromnor_2 (.in_1(notfromnor_1_out_2), .in_2(andfromnor_2_out_3), .out_3(orfromnor_2_out_3));
  andfromnor andfromnor_7 (.in_1(orfromnor_1_out_3), .in_2(notfromnor_4_out_2), .out_3(leftEngine));
  notfromnor notfromnor_4 (.in_1(andfromnor_4_out_3), .out_2(notfromnor_4_out_2));
  andfromnor andfromnor_8 (.in_1(orfromnor_2_out_3), .in_2(notfromnor_5_out_2), .out_3(andfromnor_8_out_3));
  notfromnor notfromnor_5 (.in_1(andfromnor_4_out_3), .out_2(notfromnor_5_out_2));
  orfromnor orfromnor_3 (.in_1(andfromnor_8_out_3), .in_2(andfromnor_6_out_3), .out_3(rightEngine));
endmodule

module \and  (
  input  in_1,
  input  in_2,
  input  in_3,
  input  in_4,
  output out_5
);

  wire nand_1_out, nand_2_out;

  nand nand_1 (nand_1_out, in_1, in_2, in_3, in_4);
  nand nand_2 (nand_2_out, in_1, in_2, in_3, in_4);
  nand nand_3 (out_5, nand_1_out, nand_2_out);
endmodule

module \not  (
  input  in_1,
  output out_2
);

  nand nand_1 (out_2, in_1, in_1);
endmodule

module \or  (
  input  in_1,
  input  in_2,
  input  in_3,
  input  in_4,
  output out_5
);

  wire nand_1_out, nand_2_out, nand_3_out, nand_4_out;

  nand nand_1 (nand_1_out, in_1, in_1);
  nand nand_2 (nand_2_out, in_2, in_2);
  nand nand_3 (nand_3_out, in_3, in_3);
  nand nand_4 (nand_4_out, in_4, in_4);
  nand nand_5 (out_5, nand_1_out, nand_2_out, nand_3_out, nand_4_out);
endmodule

module notfromnor (
  input  in_1,
  output out_2
);

  nor nor_1 (out_2, in_1, in_1);
endmodule

module andfromnor (
  input  in_1,
  input  in_2,
  output out_3
);

  wire nor_1_out, nor_2_out;

  nor nor_1 (nor_1_out, in_1, in_1);
  nor nor_2 (nor_2_out, in_2, in_2);
  nor nor_3 (out_3, nor_1_out, nor_2_out);
endmodule

module orfromnor (
  input  in_1,
  input  in_2,
  output out_3
);

  wire nor_1_out;

  nor nor_1 (nor_1_out, in_1, in_2);
  nor nor_2 (out_3, nor_1_out, nor_1_out);
endmodule
