// Logisim project sixth.circ as structural Verilog: 2 circuits, main circuit main
module main (
  input  [3:0] in_1,
  input  [7:0] in_2
);

  wire [7:0] rom_1_data;

  Hex_Digit_Display hex_digit_display_1 (.value(in_1));  // open: dp
  _7_Segment_Display u_7_segment_display_1 (
    .g(in_2[3]), .f(in_2[2]), .a(in_2[1]), .b(in_2[0]), .e(in_2[4]), .d(in_2[5]), .c(in_2[6]), .dp(in_2[7]));
  ROM #(.addrWidth(4)) rom_1 (.addr(in_1), .data(rom_1_data));  // open: sel
  _7_Segment_Display u_7_segment_display_2 (
    .g(rom_1_data[3]), .f(rom_1_data[2]), .a(rom_1_data[1]), .b(rom_1_data[0]), .e(rom_1_data[4]),
    .d(rom_1_data[5]), .c(rom_1_data[6]), .dp(rom_1_data[7]));

  // Notes on the sheet:
  //   contents of rom_1 (hex, n*v repeats v):
  //   77 41 3b 6b 4d 6e 7e 43 7f 4f 5f 7c 36 79 3e 1e
endmodule

module sec (
  input  norm
);

  wire clock_1_out, clock_2_out, or_1_out, or_2_out;
  wire [1:0] counter_1_q;
  wire [2:0] rom_1_data;

  Clock clock_1 (.out(clock_1_out));
  Counter #(.width(2), .max('h3)) counter_1 (
    .count(clock_1_out), .Q(counter_1_q), .clk(clock_1_out));  // open: load, D, carry, clr
  Clock clock_2 (.out(clock_2_out));
  ROM #(.addrWidth(2), .dataWidth(3)) rom_1 (.addr(counter_1_q), .data(rom_1_data), .sel(norm));
  or or_1 (or_1_out, norm, clock_2_out);
  or or_2 (or_2_out, rom_1_data[1], ~or_1_out);  // OR_Gate
  LED led_1 (.in(rom_1_data[0]));
  LED led_2 (.in(or_2_out));
  LED led_3 (.in(rom_1_data[2]));

  // Notes on the sheet:
  //   contents of rom_1 (hex, n*v repeats v):
  //   3
endmodule
