// Logisim project syc06122021.circ as structural Verilog: 3 circuits, main circuit main
module main (
  input  in_1,
  input  in_2,
  input  in_3,
  input  in_4,
  output out_5,
  output out_6
);

  wire not_1_out;

  Multiplexer #(.select(4)) multiplexer_1 (
    .in0(1'b0), .in1(1'b0), .in2(1'b1), .in3(1'b0), .in4(1'b1), .in5(1'b0), .in6(1'b0), .in7(1'b0),
    .in8(1'b0), .in9(1'b0), .in10(1'b1), .in11(1'b0), .in12(1'b0), .in13(1'b1), .in14(1'b0), .in15(1'b0),
    .out(out_5), .sel({in_4, in_3, in_2, in_1}));  // open: en
  not not_1 (not_1_out, in_1);
  Multiplexer #(.select(3)) multiplexer_2 (
    .in0(1'b0), .in1(1'b0), .in2(1'b1), .in3(1'b0), .in4(not_1_out), .in5(in_1), .in6(1'b0), .in7(1'b0),
    .out(out_6), .sel({in_4, in_3, in_2}));  // open: en
endmodule

// add_u2
module _2 (
  input  [3:0] in_1,
  input  [3:0] in_2,
  output out_3,
  output out_4,
  output out_5,
  output out_6,
  output przekroczenie
);

  wire adder_1_cout, adder_2_cout, adder_3_cout, adder_4_cout;

  Adder #(.width(1)) adder_1 (.a(in_1[0]), .b(in_2[0]), .out(out_3), .cout(adder_1_cout));  // open: cin
  Adder #(.width(1)) adder_2 (.a(in_1[1]), .b(in_2[1]), .out(out_4), .cin(adder_1_cout), .cout(adder_2_cout));
  Adder #(.width(1)) adder_3 (.a(in_1[2]), .b(in_2[2]), .out(out_5), .cin(adder_2_cout), .cout(adder_3_cout));
  Adder #(.width(1)) adder_4 (.a(in_1[3]), .b(in_2[3]), .out(out_6), .cin(adder_3_cout), .cout(adder_4_cout));
  xor xor_1 (przekroczenie, adder_3_cout, adder_4_cout);
endmodule

module _4 (
  input  [3:0] in_1,
  input  [1:0] in_2,
  input  [3:0] in_3,
  input  [3:0] in_4,
  output [3:0] out_5,
  output out_6,
  output out_7
);

  wire [3:0] and_1_out, n2_1_out_3, negator_1_out, xor_1_out;

  _2 u_2_1 (
    .in_1(in_1), .in_2(in_4), .out_3(n2_1_out_3[0]), .out_4(n2_1_out_3[1]), .out_5(n2_1_out_3[2]),
    .out_6(n2_1_out_3[3]), .przekroczenie(out_6));
  Negator #(.width(4)) negator_1 (.in(in_1), .out(negator_1_out));
  assign xor_1_out = in_1 ^ in_4;  // XOR_Gate xor_1, 4 bits wide
  assign and_1_out = in_1 & in_4;  // AND_Gate and_1, 4 bits wide
  Multiplexer #(.select(2), .width(4)) multiplexer_1 (
    .in0(n2_1_out_3), .in1(negator_1_out), .in2(xor_1_out), .in3(and_1_out), .out(out_5), .sel(in_2));  // open: en
  Comparator #(.width(4)) comparator_1 (.a(out_5), .b(in_3), .eq(out_7));  // open: gt, lt
endmodule
